// Digital circuit telnet-hello.dig as structural Verilog
module telnet_hello (
);

  wire button_1_out, telnet_1_av, telnet_1_out;

  Button button_1 (.out(button_1_out));
  Telnet telnet_1 (
    .in(8'h44), .C(button_1_out), .wr(button_1_out), .rd(telnet_1_av), .out(telnet_1_out), .av(telnet_1_av));
  // Probe on telnet_1_out
endmodule
